// Logisim project ex5.circ as structural Verilog: 5 circuits, main circuit rotr
module rotr (
  input  [15:0] A,
  input  [3:0] B,
  output [15:0] Out1
);

  wire [3:0] not_1_out;
  wire [15:0] multiplexer_1_out, multiplexer_2_out, multiplexer_3_out, rot1_1_out_2, rot2_1_out_2,
       rot4_1_out_2, rot8_1_out_2;

  assign not_1_out = ~B;  // NOT_Gate not_1, 4 bits wide
  rot1 rot1_1 (.in_1(A), .out_2(rot1_1_out_2));
  Multiplexer #(.enable("false"), .width(16)) multiplexer_1 (
    .in0(rot1_1_out_2), .in1(A), .out(multiplexer_1_out), .sel(not_1_out[0]));
  rot2 rot2_1 (.in_1(multiplexer_1_out), .out_2(rot2_1_out_2));
  Multiplexer #(.enable("false"), .width(16)) multiplexer_2 (
    .in0(rot2_1_out_2), .in1(multiplexer_1_out), .out(multiplexer_2_out), .sel(not_1_out[1]));
  rot4 rot4_1 (.in_1(multiplexer_2_out), .out_2(rot4_1_out_2));
  Multiplexer #(.enable("false"), .width(16)) multiplexer_3 (
    .in0(rot4_1_out_2), .in1(multiplexer_2_out), .out(multiplexer_3_out), .sel(not_1_out[2]));
  rot8 rot8_1 (.in_1(multiplexer_3_out), .out_2(rot8_1_out_2));
  Multiplexer #(.enable("false"), .width(16)) multiplexer_4 (
    .in0(rot8_1_out_2), .in1(multiplexer_3_out), .out(Out1), .sel(not_1_out[3]));

  // Notes on the sheet:
  //   PUT CIRCUITRY HERE
endmodule

module rot8 (
  input  [15:0] in_1,
  output [15:0] out_2
);

  wire [15:0] rot4_1_out_2;

  rot4 rot4_1 (.in_1(in_1), .out_2(rot4_1_out_2));
  rot4 rot4_2 (.in_1(rot4_1_out_2), .out_2(out_2));

  // Notes on the sheet:
  //   PUT CIRCUITRY HERE
endmodule

module rot4 (
  input  [15:0] in_1,
  output [15:0] out_2
);

  wire [15:0] rot2_1_out_2;

  rot2 rot2_1 (.in_1(in_1), .out_2(rot2_1_out_2));
  rot2 rot2_2 (.in_1(rot2_1_out_2), .out_2(out_2));

  // Notes on the sheet:
  //   PUT CIRCUITRY HERE
endmodule

module rot2 (
  input  [15:0] in_1,
  output [15:0] out_2
);

  wire [15:0] rot1_1_out_2;

  rot1 rot1_1 (.in_1(in_1), .out_2(rot1_1_out_2));
  rot1 rot1_2 (.in_1(rot1_1_out_2), .out_2(out_2));

  // Notes on the sheet:
  //   PUT CIRCUITRY HERE
endmodule

module rot1 (
  input  [15:0] in_1,
  output [15:0] out_2
);


  assign out_2 = {in_1[0], in_1[15:1]};

  // Notes on the sheet:
  //   PUT CIRCUITRY HERE
endmodule
